# Fritzing sketch HDMI (saved by Fritzing 0.9.3b)
breadboards: 1

parts:
  Raspberry_Pi_1 = Raspberry Pi 3 [part_number=RPI-3-V1.2]
  U1 = TLP621 [package=THT]
  R1 = Resistor [tolerance=±5% resistance=220 package=THT]
  S1 = Pushbutton [package="[THT]"]

nets:
  N1: Raspberry_Pi_1.GPIO27, R1.Pin_0
  N2: Raspberry_Pi_1.GND, U1.Pin_2
  N3: U1.Pin_1, R1.Pin_1
  N4: U1.Pin_4, S1.Pin_3, S1.Pin_4
  N5: U1.Pin_3, S1.Pin_1, S1.Pin_2

notes:
  HDMI切替器のタクトスイッチ
  200Ω
  フォトカプラ
